# Fritzing sketch wiring (saved by Fritzing 0.9.10b)

parts:
  Bauteil1 = Arduino Nano (Rev3.0)
  SP1 = SPEAKER [package=pcb_mount_speaker]
  BAT1 = Battery Holders [package=lipo-1100mAh]
  S2 = Round Pushbutton
  S3 = Round Pushbutton
  DFRobot_DFPlayer_Mini1 = DFRobot DFPlayer Mini [part_number=DFR0299]
  R1 = Resistor [tolerance=±5% resistance=1000 power=0.25W package="0805 [SMD]"]
  Bauteil2 = NeoPixel Stick [part_number=1426]
  R2 = Resistor [tolerance=±5% resistance=5000 power=0.25W package="0805 [SMD]"]
  R3 = Resistor [tolerance=±5% resistance=5000 power=0.25W package="0805 [SMD]"]
  S4 = Round Pushbutton
  R4 = Resistor [tolerance=±5% resistance=5000 power=0.25W package="0805 [SMD]"]
  U3 = SWITCH_SPDT [package=kps-1290]
  R5 = Resistor [tolerance=±5% resistance=220 power=0.25W package="0805 [SMD]"]
  LED2 = LED - 3mm [color="Red (633nm)" current=0.030 package="3 mm [THT]"]
  Bauteil3 = NeoPixel Stick [part_number=1426]
  Bauteil4 = NeoPixel Stick [part_number=1426]

nets:
  GND: Bauteil1.GND, BAT1.-, DFRobot_DFPlayer_Mini1.GND-2, Bauteil2.GND, R2.Pin_1, R3.Pin_1, R4.Pin_1, LED2.cathode, Bauteil3.GND, Bauteil4.GND
  N1: Bauteil1.D5, Bauteil3.DATAIN
  N2: Bauteil1.D6, Bauteil4.DATAIN
  N3: Bauteil1.D7, S2.leg1, R2.Pin_0
  N4: Bauteil1.D8, S3.leg1, R3.Pin_0
  N5: Bauteil1.D9, Bauteil2.DATAIN
  N6: Bauteil1.D10, DFRobot_DFPlayer_Mini1.TX
  N7: Bauteil1.D11/MOSI, R1.Pin_0
  N8: Bauteil1.D12/MISO, S4.leg1, R4.Pin_0
  +5V: Bauteil1.5V, S2.leg0, S3.leg0, DFRobot_DFPlayer_Mini1.VCC, Bauteil2.+5V, S4.leg0, U3.S, R5.Pin_0, Bauteil3.+5V, Bauteil4.+5V
  N9: SP1.+, DFRobot_DFPlayer_Mini1.SPK_2
  N10: SP1.-, DFRobot_DFPlayer_Mini1.SPK_1
  N11: BAT1.+, U3.O
  N12: DFRobot_DFPlayer_Mini1.RX, R1.Pin_1
  N13: R5.Pin_1, LED2.anode

notes:
  Trigger
  Sound Selector
  Color Selector
  Power
  Light System
  Sound System
  Front
  Button System
  Right
  Left

custom parts:
  NeoPixel Stick: Make your own little LED strip arrangement with this stick of NeoPixel LEDs. We crammed 8 of the tiny 5050 (5mm x 5mm) smart RGB LEDs onto a PCB with mounting holes and a chainable design. Use only one microcontroller pin to control as many as you can chain together! Each LED is addressable as the driver chip is inside the LED. Each one has ~18mA constant current drive so the color will be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
